# Fritzing sketch Arduino_circuit (saved by Fritzing 0.8.7b)
circuit board: 6.9215cm x 5.33756cm
breadboards: 1

parts:
  JP1 = Header 3 [package=molex-1x3_lock]
  R1 = Resistor [tolerance=±0.1% resistance=10k package=THT]
  JP3 = Header 2 [package=molex-1x2_lock]
  Part2 = Arduino Ethernet Shield (Rev3)

nets:
  N1: JP1.1, R1.Pin_1, Part2.D2
  N2: JP1.3, JP3.1, Part2.GND
  N3: R1.Pin_0, Part2.5V
  N4: JP3.2, Part2.SDCS
