# Fritzing sketch Arduino_circuit_2 (saved by Fritzing 0.9.2b)
circuit board: 6.9215cm x 5.33756cm
breadboards: 1

parts:
  Relay = Header 2 [package=molex-1x2_lock]
  Flow_2 = Header 3 [package=molex-1x3_lock]
  R2 = Resistor [tolerance=±0.1% resistance=10k package=THT]
  Flow_3 = Header 3 [package=molex-1x3_lock]
  R3 = Resistor [tolerance=±0.1% resistance=10k package=THT]
  +12V = Header 2 [package=molex-1x2_lock]
  Flow_1 = Header 3 [package=molex-1x3_lock]
  R1 = Resistor [tolerance=±0.1% resistance=10k package=THT]
  Part1 = Arduino Ethernet Shield (Rev3)

nets:
  N1: Relay.1, Flow_2.3, Flow_3.3, +12V.1, Flow_1.3, Part1.GND
  N2: Relay.2, Part1.PWM_D11
  N3: Flow_2.1, R2.Pin_1, Part1.D7
  N4: Flow_2.2, Flow_3.2, +12V.2, Flow_1.2
  N5: R2.Pin_0, R3.Pin_0, R1.Pin_0, Part1.5V
  N6: Flow_3.1, R3.Pin_1, Part1.D8
  N7: Flow_1.1, R1.Pin_1, Part1.D2
